# Fritzing sketch pcdDesign (saved by Fritzing 0.9.3b)
circuit board: 8.46667cm x 5.64444cm
breadboards: 1

parts:
  U1 = NodeMCU V1.0
  GY1 = MPU-6050 Board GY-521 [form="♀ (female)" package=THT]
  R1 = Resistor [tolerance=±5% resistance=220 package=THT]
  R2 = Resistor [tolerance=±5% resistance=220 package=THT]
  LED1 = RGB LED (com. cathode, rgb) [package="5 mm [THT]"]
  R3 = Resistor [tolerance=±5% resistance=220 package=THT]
  R4 = Resistor [tolerance=±5% resistance=220 package=THT]
  R5 = Resistor [tolerance=±5% resistance=220 package=THT]

nets:
  N1: U1.D1, R5.Pin_1
  N2: U1.D2, R4.Pin_1
  N3: U1.D3, R3.Pin_1
  N4: U1.GND, GY1.pin2, R2.Pin_0, LED1.common_cathode
  N5: U1.D5, GY1.pin4
  N6: U1.D6, GY1.pin3
  N7: U1.Vin, GY1.pin1, R1.Pin_1
  N8: U1.A0, R1.Pin_0, R2.Pin_1
  N9: LED1.red_anode, R3.Pin_0
  N10: LED1.green_anode, R4.Pin_0
  N11: LED1.blue_anode, R5.Pin_0

custom parts:
  NodeMCU V1.0: ESP8266 based NodeMCU
  MPU-6050 Board GY-521: Acelerometro y Giroscopio MPU-6050 Board GY-521
